// Logisim project DigitalDesignProject.circ as structural Verilog: 18 circuits, main circuit main
module main (
  input  RESET
);

  wire Branch_Control_Unit_mux6, clock_1_out, control_unit_1_memread, control_unit_1_memwrt,
       control_unit_1_mux1, control_unit_1_mux3, control_unit_1_mux4, control_unit_1_mux5,
       control_unit_1_mux6, control_unit_1_pcread, control_unit_1_pcwrite, control_unit_1_we, or_1_out;
  wire [1:0] control_unit_1_mux2;
  wire [2:0] control_unit_1_branchcontrolinput;
  wire [3:0] control_unit_1_rd1, control_unit_1_rd2, control_unit_1_wr;
  wire [9:0] n18to10_1_out_2;
  wire [17:0] Adder_2_outdata, Adder_3_outdata, Adder_outdata, alu_1_out, multiplexer_1_out,
       multiplexer_2_out, multiplexer_3_out, multiplexer_4_out, multiplexer_5_out, multiplexer_6_out,
       program_counter_1_out_6, ram_1_data, register_file_1_outdata1, register_file_1_outdata2, rom_1_data,
       S_Ext6to18_out_2, Sign14to18_out_2, SignEx6to18_out_2;

  Clock clock_1 (.out(clock_1_out));
  Program_Counter program_counter_1 (
    .Set(control_unit_1_pcread), .Write(control_unit_1_pcwrite), .in_3(multiplexer_2_out), .Reset(RESET),
    .Clk(clock_1_out), .out_6(program_counter_1_out_6));
  ROM #(.addrWidth(18), .dataWidth(18)) rom_1 (.addr(program_counter_1_out_6), .data(rom_1_data), .sel(1'b1));
  SignExtend6to18 S_Ext6to18 (.in_1(rom_1_data), .out_2(S_Ext6to18_out_2));
  SignExtend14to18 Sign14to18 (.in_1(rom_1_data), .out_2(Sign14to18_out_2));
  SignExtend6to18 SignEx6to18 (.in_1(rom_1_data), .out_2(SignEx6to18_out_2));
  Control_Unit control_unit_1 (
    .Instruction(rom_1_data), .rd1(control_unit_1_rd1), .rd2(control_unit_1_rd2), .wr(control_unit_1_wr),
    .Clk(clock_1_out), .MUX1(control_unit_1_mux1), .MUX2(control_unit_1_mux2), .MUX4(control_unit_1_mux4),
    .MUX3(control_unit_1_mux3), .MUX5(control_unit_1_mux5), .MemRead(control_unit_1_memread),
    .MemWrt(control_unit_1_memwrt), .WE(control_unit_1_we), .pcRead(control_unit_1_pcread),
    .pcWrite(control_unit_1_pcwrite), .BranchControlInput(control_unit_1_branchcontrolinput),
    .mux6(control_unit_1_mux6));
  Register_File register_file_1 (
    .rd1(control_unit_1_rd2), .rd2(control_unit_1_rd1), .IN_DATA(multiplexer_5_out), .Wr(control_unit_1_wr),
    .Clk(clock_1_out), .WE(control_unit_1_we), .OutData2(register_file_1_outdata2),
    .OutData1(register_file_1_outdata1));
  _18to10 u_18to10_1 (.in_1(rom_1_data), .out_2(n18to10_1_out_2));
  Multiplexer #(.width(18), .enable("false")) multiplexer_1 (
    .in0(register_file_1_outdata2), .in1(S_Ext6to18_out_2), .out(multiplexer_1_out), .sel(control_unit_1_mux1));
  _18Bit_Adder Adder (.OutData(Adder_outdata), .InData1(SignEx6to18_out_2), .InData2(program_counter_1_out_6));
  ALU alu_1 (
    .OpCode(rom_1_data[17:14]), .InData1(multiplexer_1_out), .InData2(register_file_1_outdata1),
    .OUT(alu_1_out));
  _18Bit_Adder Adder_2 (.OutData(Adder_2_outdata), .InData1(Sign14to18_out_2), .InData2(program_counter_1_out_6));
  _18Bit_Adder Adder_3 (.OutData(Adder_3_outdata), .InData1(program_counter_1_out_6), .InData2(18'h1));
  Multiplexer #(.width(18), .enable("false")) multiplexer_2 (
    .in0(Adder_3_outdata), .in1(multiplexer_6_out), .out(multiplexer_2_out), .sel(or_1_out));
  Branch_Control_Unit Branch_Control_Unit (
    .nzp(control_unit_1_branchcontrolinput), .op1(register_file_1_outdata2), .op2(register_file_1_outdata1),
    .MUX6(Branch_Control_Unit_mux6));
  or or_1 (or_1_out, control_unit_1_mux6, Branch_Control_Unit_mux6);
  Multiplexer #(.select(2), .width(18), .enable("false")) multiplexer_3 (
    .in0(alu_1_out), .in1({18{1'b1}}), .in2(Adder_outdata), .in3(Adder_2_outdata), .out(multiplexer_3_out),
    .sel(control_unit_1_mux2));
  RAM #(.addrWidth(10), .dataWidth(18), .bus("separate")) ram_1 (
    .addr(n18to10_1_out_2), .din(register_file_1_outdata2), .data(ram_1_data), .str(control_unit_1_memwrt),
    .sel(1'b1), .clk(clock_1_out), .ld(control_unit_1_memread), .clr(1'b0));
  Multiplexer #(.width(18), .enable("false")) multiplexer_4 (
    .in0(ram_1_data), .in1(multiplexer_3_out), .out(multiplexer_4_out), .sel(control_unit_1_mux3));
  Multiplexer #(.width(18), .enable("false")) multiplexer_5 (
    .in0(multiplexer_4_out), .in1(Adder_3_outdata), .out(multiplexer_5_out), .sel(control_unit_1_mux4));
  Multiplexer #(.width(18), .enable("false")) multiplexer_6 (
    .in0(multiplexer_4_out), .in1(Adder_3_outdata), .out(multiplexer_6_out), .sel(control_unit_1_mux5));

  // Notes on the sheet:
  //   Instruction Memo
  //   contents of rom_1 (hex, n*v repeats v):
  //   14003 0 0 24483 20bc4 24fcc 25394 25754 9142 0 0 0 90c3 0 29914 2dd14 3204c 3644c 3a84c 3ec4c 50c3
  //   4*0 4d02 0 0 0 104c3 4*0 10c42 0 0 0 d143 4*0 cd04 5*0 c542 6*0 19143 4*0 18544 6*0 19442 0 0 0
  //   1c401 2401 17ffe
  //   ALU IMM
  //   Ld/St
  //   Jump
  //   Branch
  //   MUX1
  //   MUX6
  //   to control unt
  //   MUX2
  //   to cont unt
  //   Data Memory
  //   to cont unt
  //   MUX3
  //   to cont unt
  //   MUX4
  //   to cont unt
  //   MUX5
endmodule

// DLatch
module D_Latch (
  input  D,
  input  clk,
  output out_3,
  output out_4
);

  wire and_1_out, and_2_out, not_1_out;

  not not_1 (not_1_out, D);
  and and_1 (and_1_out, D, clk);
  and and_2 (and_2_out, clk, not_1_out);
  nor nor_1 (out_3, and_1_out, out_4);
  nor nor_2 (out_4, out_3, and_2_out);
endmodule

module Register_File (
  input  [3:0] rd1,
  input  [3:0] rd2,
  input  [17:0] IN_DATA,
  input  [3:0] Wr,
  input  WE,
  input  Clk,
  output [17:0] OutData2,
  output [17:0] OutData1
);

  wire and_1_out, and_2_out, and_3_out, and_4_out, and_5_out, and_6_out, and_7_out, and_8_out, and_9_out,
       and_10_out, and_11_out, and_12_out, and_13_out, and_14_out, and_15_out, and_16_out, decoder_1_out0,
       decoder_1_out1, decoder_1_out2, decoder_1_out3, decoder_1_out4, decoder_1_out5, decoder_1_out6,
       decoder_1_out7, decoder_1_out8, decoder_1_out9, decoder_1_out10, decoder_1_out11, decoder_1_out12,
       decoder_1_out13, decoder_1_out14, decoder_1_out15, decoder_2_out0, decoder_2_out1, decoder_2_out2,
       decoder_2_out3, decoder_2_out4, decoder_2_out5, decoder_2_out6, decoder_2_out7, decoder_2_out8,
       decoder_2_out9, decoder_2_out10, decoder_2_out11, decoder_2_out12, decoder_2_out13, decoder_2_out14,
       decoder_2_out15, decoder_3_out0, decoder_3_out1, decoder_3_out2, decoder_3_out3, decoder_3_out4,
       decoder_3_out5, decoder_3_out6, decoder_3_out7, decoder_3_out8, decoder_3_out9, decoder_3_out10,
       decoder_3_out11, decoder_3_out12, decoder_3_out13, decoder_3_out14, decoder_3_out15;
  wire [17:0] register_1_q, register_2_q, register_3_q, register_4_q, register_5_q, register_6_q,
       register_7_q, register_8_q, register_9_q, register_10_q, register_11_q, register_12_q, register_13_q,
       register_14_q, register_15_q, register_16_q;

  Decoder #(.select(4)) decoder_1 (
    .out0(decoder_1_out0), .out1(decoder_1_out1), .out2(decoder_1_out2), .out3(decoder_1_out3),
    .out4(decoder_1_out4), .out5(decoder_1_out5), .out6(decoder_1_out6), .out7(decoder_1_out7),
    .out8(decoder_1_out8), .out9(decoder_1_out9), .out10(decoder_1_out10), .out11(decoder_1_out11),
    .out12(decoder_1_out12), .out13(decoder_1_out13), .out14(decoder_1_out14), .out15(decoder_1_out15),
    .sel(rd1));  // open: en
  Decoder #(.select(4)) decoder_2 (
    .out0(decoder_2_out0), .out1(decoder_2_out1), .out2(decoder_2_out2), .out3(decoder_2_out3),
    .out4(decoder_2_out4), .out5(decoder_2_out5), .out6(decoder_2_out6), .out7(decoder_2_out7),
    .out8(decoder_2_out8), .out9(decoder_2_out9), .out10(decoder_2_out10), .out11(decoder_2_out11),
    .out12(decoder_2_out12), .out13(decoder_2_out13), .out14(decoder_2_out14), .out15(decoder_2_out15),
    .sel(rd2));  // open: en
  Decoder #(.select(4)) decoder_3 (
    .out0(decoder_3_out0), .out1(decoder_3_out1), .out2(decoder_3_out2), .out3(decoder_3_out3),
    .out4(decoder_3_out4), .out5(decoder_3_out5), .out6(decoder_3_out6), .out7(decoder_3_out7),
    .out8(decoder_3_out8), .out9(decoder_3_out9), .out10(decoder_3_out10), .out11(decoder_3_out11),
    .out12(decoder_3_out12), .out13(decoder_3_out13), .out14(decoder_3_out14), .out15(decoder_3_out15),
    .sel(Wr));  // open: en
  and and_1 (and_1_out, decoder_3_out0, WE);
  and and_2 (and_2_out, decoder_3_out1, WE);
  and and_3 (and_3_out, decoder_3_out2, WE);
  and and_4 (and_4_out, decoder_3_out3, WE);
  and and_5 (and_5_out, decoder_3_out4, WE);
  and and_6 (and_6_out, decoder_3_out5, WE);
  and and_7 (and_7_out, decoder_3_out6, WE);
  and and_8 (and_8_out, decoder_3_out7, WE);
  and and_9 (and_9_out, decoder_3_out8, WE);
  and and_10 (and_10_out, decoder_3_out9, WE);
  and and_11 (and_11_out, decoder_3_out10, WE);
  and and_12 (and_12_out, decoder_3_out11, WE);
  and and_13 (and_13_out, decoder_3_out12, WE);
  and and_14 (and_14_out, decoder_3_out13, WE);
  and and_15 (and_15_out, decoder_3_out14, WE);
  and and_16 (and_16_out, decoder_3_out15, WE);
  Register #(.width(18)) register_1 (.D(IN_DATA), .en(and_1_out), .Q(register_1_q), .clk(Clk), .clr(1'b0));
  Register #(.width(18)) register_2 (.D(IN_DATA), .en(and_2_out), .Q(register_2_q), .clk(Clk), .clr(1'b0));
  Register #(.width(18)) register_3 (.D(IN_DATA), .en(and_3_out), .Q(register_3_q), .clk(Clk), .clr(1'b0));
  Register #(.width(18)) register_4 (.D(IN_DATA), .en(and_4_out), .Q(register_4_q), .clk(Clk), .clr(1'b0));
  Register #(.width(18)) register_5 (.D(IN_DATA), .en(and_5_out), .Q(register_5_q), .clk(Clk), .clr(1'b0));
  Register #(.width(18)) register_6 (.D(IN_DATA), .en(and_6_out), .Q(register_6_q), .clk(Clk), .clr(1'b0));
  Register #(.width(18)) register_7 (.D(IN_DATA), .en(and_7_out), .Q(register_7_q), .clk(Clk), .clr(1'b0));
  Register #(.width(18)) register_8 (.D(IN_DATA), .en(and_8_out), .Q(register_8_q), .clk(Clk), .clr(1'b0));
  Register #(.width(18)) register_9 (.D(IN_DATA), .en(and_9_out), .Q(register_9_q), .clk(Clk), .clr(1'b0));
  Register #(.width(18)) register_10 (.D(IN_DATA), .en(and_10_out), .Q(register_10_q), .clk(Clk), .clr(1'b0));
  Register #(.width(18)) register_11 (.D(IN_DATA), .en(and_11_out), .Q(register_11_q), .clk(Clk), .clr(1'b0));
  Register #(.width(18)) register_12 (.D(IN_DATA), .en(and_12_out), .Q(register_12_q), .clk(Clk), .clr(1'b0));
  Register #(.width(18)) register_13 (.D(IN_DATA), .en(and_13_out), .Q(register_13_q), .clk(Clk), .clr(1'b0));
  Register #(.width(18)) register_14 (.D(IN_DATA), .en(and_14_out), .Q(register_14_q), .clk(Clk), .clr(1'b0));
  Register #(.width(18)) register_15 (.D(IN_DATA), .en(and_15_out), .Q(register_15_q), .clk(Clk), .clr(1'b0));
  Register #(.width(18)) register_16 (.D(IN_DATA), .en(and_16_out), .Q(register_16_q), .clk(Clk), .clr(1'b0));
  assign OutData2 = decoder_2_out0 ? register_1_q : 18'bz;  // Controlled_Buffer controlled_buffer_1
  assign OutData1 = decoder_1_out0 ? register_1_q : 18'bz;  // Controlled_Buffer controlled_buffer_2
  assign OutData2 = decoder_2_out1 ? register_2_q : 18'bz;  // Controlled_Buffer controlled_buffer_3
  assign OutData1 = decoder_1_out1 ? register_2_q : 18'bz;  // Controlled_Buffer controlled_buffer_4
  assign OutData2 = decoder_2_out2 ? register_3_q : 18'bz;  // Controlled_Buffer controlled_buffer_5
  assign OutData1 = decoder_1_out2 ? register_3_q : 18'bz;  // Controlled_Buffer controlled_buffer_6
  assign OutData2 = decoder_2_out3 ? register_4_q : 18'bz;  // Controlled_Buffer controlled_buffer_7
  assign OutData1 = decoder_1_out3 ? register_4_q : 18'bz;  // Controlled_Buffer controlled_buffer_8
  assign OutData2 = decoder_2_out4 ? register_5_q : 18'bz;  // Controlled_Buffer controlled_buffer_9
  assign OutData1 = decoder_1_out4 ? register_5_q : 18'bz;  // Controlled_Buffer controlled_buffer_10
  assign OutData2 = decoder_2_out5 ? register_6_q : 18'bz;  // Controlled_Buffer controlled_buffer_11
  assign OutData1 = decoder_1_out5 ? register_6_q : 18'bz;  // Controlled_Buffer controlled_buffer_12
  assign OutData2 = decoder_2_out6 ? register_7_q : 18'bz;  // Controlled_Buffer controlled_buffer_13
  assign OutData1 = decoder_1_out6 ? register_7_q : 18'bz;  // Controlled_Buffer controlled_buffer_14
  assign OutData2 = decoder_2_out7 ? register_8_q : 18'bz;  // Controlled_Buffer controlled_buffer_15
  assign OutData1 = decoder_1_out7 ? register_8_q : 18'bz;  // Controlled_Buffer controlled_buffer_16
  assign OutData2 = decoder_2_out8 ? register_9_q : 18'bz;  // Controlled_Buffer controlled_buffer_17
  assign OutData1 = decoder_1_out8 ? register_9_q : 18'bz;  // Controlled_Buffer controlled_buffer_18
  assign OutData2 = decoder_2_out9 ? register_10_q : 18'bz;  // Controlled_Buffer controlled_buffer_19
  assign OutData1 = decoder_1_out9 ? register_10_q : 18'bz;  // Controlled_Buffer controlled_buffer_20
  assign OutData2 = decoder_2_out10 ? register_11_q : 18'bz;  // Controlled_Buffer controlled_buffer_21
  assign OutData1 = decoder_1_out10 ? register_11_q : 18'bz;  // Controlled_Buffer controlled_buffer_22
  assign OutData2 = decoder_2_out11 ? register_12_q : 18'bz;  // Controlled_Buffer controlled_buffer_23
  assign OutData1 = decoder_1_out11 ? register_12_q : 18'bz;  // Controlled_Buffer controlled_buffer_24
  assign OutData2 = decoder_2_out12 ? register_13_q : 18'bz;  // Controlled_Buffer controlled_buffer_25
  assign OutData1 = decoder_1_out12 ? register_13_q : 18'bz;  // Controlled_Buffer controlled_buffer_26
  assign OutData2 = decoder_2_out13 ? register_14_q : 18'bz;  // Controlled_Buffer controlled_buffer_27
  assign OutData1 = decoder_1_out13 ? register_14_q : 18'bz;  // Controlled_Buffer controlled_buffer_28
  assign OutData2 = decoder_2_out14 ? register_15_q : 18'bz;  // Controlled_Buffer controlled_buffer_29
  assign OutData1 = decoder_1_out14 ? register_15_q : 18'bz;  // Controlled_Buffer controlled_buffer_30
  assign OutData2 = decoder_2_out15 ? register_16_q : 18'bz;  // Controlled_Buffer controlled_buffer_31
  assign OutData1 = decoder_1_out15 ? register_16_q : 18'bz;  // Controlled_Buffer controlled_buffer_32
endmodule

module D_Flip_Flop (
  input  D,
  input  CLK,
  input  EN,
  output Q_prime,
  output Q
);

  wire and_1_out, Master_out_3, not_1_out;

  and and_1 (and_1_out, CLK, EN);
  not not_1 (not_1_out, and_1_out);
  D_Latch Master (.D(D), .clk(not_1_out), .out_3(Master_out_3));  // open: out_4
  D_Latch Servant (.D(Master_out_3), .clk(and_1_out), .out_3(Q_prime), .out_4(Q));
endmodule

module Adder (
  input  A,
  input  B,
  input  C,
  output Sum,
  output Carry
);

  wire and_1_out, and_2_out, xor_1_out;

  xor xor_1 (xor_1_out, A, B);
  xor xor_2 (Sum, xor_1_out, C);
  and and_1 (and_1_out, xor_1_out, C);
  and and_2 (and_2_out, A, B);
  or or_1 (Carry, and_1_out, and_2_out);
endmodule

module _18Bit_Adder (
  input  [17:0] InData1,
  input  [17:0] InData2,
  output [17:0] OutData
);

  wire adder_1_carry, adder_2_carry, adder_3_carry, adder_4_carry, adder_5_carry, adder_6_carry,
       adder_7_carry, adder_8_carry, adder_9_carry, adder_10_carry, adder_11_carry, adder_12_carry,
       adder_13_carry, adder_14_carry, adder_15_carry, adder_16_carry, adder_17_carry, adder_18_carry;

  Adder adder_1 (.A(InData2[17]), .B(InData1[17]), .C(adder_2_carry), .Sum(OutData[17]), .Carry(adder_1_carry));
  Adder adder_2 (.A(InData2[16]), .B(InData1[16]), .C(adder_3_carry), .Sum(OutData[16]), .Carry(adder_2_carry));
  Adder adder_3 (.A(InData2[15]), .B(InData1[15]), .C(adder_4_carry), .Sum(OutData[15]), .Carry(adder_3_carry));
  Adder adder_4 (.A(InData2[14]), .B(InData1[14]), .C(adder_5_carry), .Sum(OutData[14]), .Carry(adder_4_carry));
  Adder adder_5 (.A(InData2[13]), .B(InData1[13]), .C(adder_6_carry), .Sum(OutData[13]), .Carry(adder_5_carry));
  Adder adder_6 (.A(InData2[12]), .B(InData1[12]), .C(adder_7_carry), .Sum(OutData[12]), .Carry(adder_6_carry));
  Adder adder_7 (.A(InData2[11]), .B(InData1[11]), .C(adder_8_carry), .Sum(OutData[11]), .Carry(adder_7_carry));
  Adder adder_8 (.A(InData2[10]), .B(InData1[10]), .C(adder_10_carry), .Sum(OutData[10]), .Carry(adder_8_carry));
  Adder adder_9 (.A(InData2[8]), .B(InData1[8]), .C(adder_11_carry), .Sum(OutData[8]), .Carry(adder_9_carry));
  Adder adder_10 (.A(InData2[9]), .B(InData1[9]), .C(adder_9_carry), .Sum(OutData[9]), .Carry(adder_10_carry));
  Adder adder_11 (.A(InData2[7]), .B(InData1[7]), .C(adder_12_carry), .Sum(OutData[7]), .Carry(adder_11_carry));
  Adder adder_12 (.A(InData2[6]), .B(InData1[6]), .C(adder_13_carry), .Sum(OutData[6]), .Carry(adder_12_carry));
  Adder adder_13 (.A(InData2[5]), .B(InData1[5]), .C(adder_14_carry), .Sum(OutData[5]), .Carry(adder_13_carry));
  Adder adder_14 (.A(InData2[4]), .B(InData1[4]), .C(adder_15_carry), .Sum(OutData[4]), .Carry(adder_14_carry));
  Adder adder_15 (.A(InData2[3]), .B(InData1[3]), .C(adder_16_carry), .Sum(OutData[3]), .Carry(adder_15_carry));
  Adder adder_16 (.A(InData2[2]), .B(InData1[2]), .C(adder_18_carry), .Sum(OutData[2]), .Carry(adder_16_carry));
  Adder adder_17 (.A(InData2[0]), .B(InData1[0]), .C(1'b0), .Sum(OutData[0]), .Carry(adder_17_carry));
  Adder adder_18 (.A(InData2[1]), .B(InData1[1]), .C(adder_17_carry), .Sum(OutData[1]), .Carry(adder_18_carry));

  // Notes on the sheet:
  //   Empty
endmodule

module ALU (
  input  [17:0] InData1,
  input  [17:0] InData2,
  input  [3:0] OpCode,
  output [17:0] OUT
);

  wire ADD_out, ADDI_out, AND_2_out, ANDI_out, not_1_out, not_2_out, not_3_out, not_4_out, not_5_out,
       not_6_out, not_7_out, not_8_out, not_9_out, not_10_out, not_11_out, not_12_out, OR_2_out, ORI_out,
       XOR_2_out, XORI_out;
  wire [3:0] or_3_out;
  wire [17:0] and_1_out, n18bit_adder_1_outdata, or_1_out, xor_1_out;

  _18Bit_Adder u_18bit_adder_1 (.OutData(n18bit_adder_1_outdata), .InData1(InData1), .InData2(InData2));
  assign and_1_out = InData1 & InData2;  // AND_Gate and_1, 18 bits wide
  assign or_1_out = InData1 | InData2;  // OR_Gate or_1, 18 bits wide
  assign xor_1_out = InData1 ^ InData2;  // XOR_Gate xor_1, 18 bits wide
  not not_1 (not_1_out, OpCode[0]);
  not not_2 (not_2_out, OpCode[1]);
  not not_3 (not_3_out, OpCode[2]);
  not not_4 (not_4_out, OpCode[1]);
  not not_5 (not_5_out, OpCode[2]);
  not not_6 (not_6_out, OpCode[0]);
  not not_7 (not_7_out, OpCode[2]);
  not not_8 (not_8_out, OpCode[2]);
  not not_9 (not_9_out, OpCode[0]);
  not not_10 (not_10_out, OpCode[1]);
  not not_11 (not_11_out, OpCode[1]);
  not not_12 (not_12_out, OpCode[0]);
  and ADD (ADD_out, not_1_out, not_2_out, not_3_out, OpCode[3]);
  and ADDI (ADDI_out, OpCode[0], not_4_out, not_5_out, OpCode[3]);
  and AND_2 (AND_2_out, not_6_out, OpCode[1], not_7_out, OpCode[3]);
  and ANDI (ANDI_out, OpCode[0], OpCode[1], not_8_out, OpCode[3]);
  and OR_2 (OR_2_out, not_9_out, not_10_out, OpCode[2], OpCode[3]);
  and ORI (ORI_out, OpCode[0], not_11_out, OpCode[2], OpCode[3]);
  and XOR_2 (XOR_2_out, not_12_out, OpCode[1], OpCode[2], OpCode[3]);
  and XORI (XORI_out, OpCode[0], OpCode[1], OpCode[2], OpCode[3]);
  or or_3 (or_3_out[0], ADD_out, ADDI_out);
  or or_4 (or_3_out[1], AND_2_out, ANDI_out);
  or or_5 (or_3_out[2], OR_2_out, ORI_out);
  or or_6 (or_3_out[3], XOR_2_out, XORI_out);
  Multiplexer #(.select(4), .width(18), .enable("false")) multiplexer_1 (
    .in0({18{1'b1}}), .in1(n18bit_adder_1_outdata), .in2(and_1_out), .in4(or_1_out), .in8(xor_1_out),
    .out(OUT), .sel(or_3_out));  // open: in3, in5, in6, in7, in9, in10, in11, in12, in13, in14, in15
endmodule

// PC
module Program_Counter (
  input  Set,
  input  Write,
  input  [17:0] in_3,
  input  Reset,
  input  Clk,
  output [17:0] out_6
);

  wire [17:0] multiplexer_1_out;

  Multiplexer #(.width(18)) multiplexer_1 (.in0(out_6), .in1(in_3), .out(multiplexer_1_out), .sel(Write));  // open: en
  Register #(.width(18)) register_1 (.D(multiplexer_1_out), .en(Set), .Q(out_6), .clk(Clk), .clr(Reset));
endmodule

module SignExtend14to18 (
  input  [17:0] in_1,
  output [17:0] out_2
);

  Multiplexer #(.width(4)) multiplexer_1 (
    .in0(4'b0000), .in1(4'b1111), .out(out_2[17:14]), .sel(in_1[13]));  // open: en

  assign out_2[13:0] = in_1[13:0];
endmodule

module ZeroExtend6to18 (
  input  [17:0] in_1,
  output [17:0] out_2
);


  assign out_2 = {{12{1'b0}}, in_1[5:0]};
endmodule

module SignExtend6to18 (
  input  [17:0] in_1,
  output [17:0] out_2
);

  Multiplexer #(.width(12)) multiplexer_1 (
    .in0({12{1'b0}}), .in1({12{1'b1}}), .out(out_2[17:6]), .sel(in_1[5]));  // open: en

  assign out_2[5:0] = in_1[5:0];
endmodule

module ZeroExtend10to18 (
  input  [17:0] in_1,
  output [17:0] out_2
);


  assign out_2 = {{8{1'b0}}, in_1[9:0]};
endmodule

module Control_Unit (
  input  [17:0] Instruction,
  input  Clk,
  output MUX1,
  output [1:0] MUX2,
  output MUX4,
  output MUX3,
  output MUX5,
  output MemRead,
  output MemWrt,
  output WE,
  output pcRead,
  output pcWrite,
  output [3:0] rd1,
  output [3:0] rd2,
  output [3:0] wr,
  output [2:0] BranchControlInput,
  output mux6
);

  wire alu_normal_out, alu_out, and_1_out, Beq_out, Bge_2_out, Bge_out, bgt_2_out, Bgt_out, Blt_out, Br_out,
       decoder_1_out0, decoder_1_out1, decoder_1_out2, decoder_1_out3, decoder_1_out4, decoder_1_out5,
       decoder_1_out6, decoder_1_out8, decoder_1_out9, decoder_1_out10, decoder_1_out11, decoder_1_out12,
       decoder_1_out13, decoder_1_out14, decoder_1_out15, ld_st_out, not_1_out, not_2_out, not_3_out,
       not_4_out, not_5_out, not_6_out, not_7_out, not_8_out, not_9_out, not_10_out, not_11_out, not_12_out,
       not_13_out, not_14_out, not_15_out, not_16_out, not_17_out, not_18_out, not_19_out, not_20_out,
       not_21_out, not_22_out, not_23_out, not_24_out, or_1_out, or_2_out, or_3_out, register_1_q, St_out;
  wire [3:0] counter_1_q;

  assign rd2 = or_1_out ? Instruction[9:6] : 4'bz;  // Controlled_Buffer controlled_buffer_1
  assign rd2 = not_1_out ? Instruction[5:2] : 4'bz;  // Controlled_Buffer controlled_buffer_2
  not not_1 (not_1_out, or_1_out);
  assign rd1 = or_2_out ? Instruction[13:10] : 4'bz;  // Controlled_Buffer controlled_buffer_3
  not not_2 (not_2_out, or_2_out);
  assign rd1 = not_2_out ? Instruction[5:2] : 4'bz;  // Controlled_Buffer controlled_buffer_4
  or or_1 (or_1_out, Beq_out, Bgt_out, Blt_out, Bge_out, Bge_2_out);
  or or_2 (or_2_out, St_out, or_1_out);
  and Beq (Beq_out, not_4_out, Instruction[15], not_5_out, not_6_out);
  and Bgt (Bgt_out, Instruction[14], not_7_out, not_8_out, not_9_out);
  and Blt (Blt_out, not_10_out, not_11_out, Instruction[16], not_12_out);
  and Bge (Bge_out, Instruction[14], Instruction[15], not_13_out, not_14_out);
  and Bge_2 (Bge_2_out, not_15_out, Instruction[15], Instruction[16], not_16_out);
  and St (St_out, Instruction[14], Instruction[15], Instruction[16], not_3_out);
  not not_3 (not_3_out, Instruction[17]);
  not not_4 (not_4_out, Instruction[14]);
  not not_5 (not_5_out, Instruction[16]);
  not not_6 (not_6_out, Instruction[17]);
  not not_7 (not_7_out, Instruction[15]);
  not not_8 (not_8_out, Instruction[16]);
  not not_9 (not_9_out, Instruction[17]);
  not not_10 (not_10_out, Instruction[14]);
  not not_11 (not_11_out, Instruction[15]);
  not not_12 (not_12_out, Instruction[17]);
  not not_13 (not_13_out, Instruction[16]);
  not not_14 (not_14_out, Instruction[17]);
  not not_15 (not_15_out, Instruction[14]);
  not not_16 (not_16_out, Instruction[17]);
  not not_17 (not_17_out, Instruction[14]);
  not not_18 (not_18_out, Instruction[15]);
  not not_19 (not_19_out, Instruction[16]);
  not not_20 (not_20_out, Instruction[17]);
  Counter #(.width(4), .max('hf)) counter_1 (
    .load(decoder_1_out1), .D(Instruction[17:14]), .count(or_3_out), .Q(counter_1_q), .clk(Clk),
    .clr(and_1_out));  // open: carry
  and and_1 (and_1_out, not_21_out, register_1_q);
  not not_21 (not_21_out, or_3_out);
  Register #(.width(1)) register_1 (.D(pcWrite), .en(1'b1), .Q(register_1_q), .clk(Clk), .clr(1'b0));
  or or_3 (or_3_out, decoder_1_out0, MemRead);
  and ld (MemRead, not_17_out, not_18_out, not_19_out, not_20_out);
  not not_22 (not_22_out, Instruction[15]);
  and bgt_2 (bgt_2_out, Instruction[14], not_22_out, not_23_out, not_24_out);
  not not_23 (not_23_out, Instruction[16]);
  not not_24 (not_24_out, Instruction[17]);
  Decoder #(.select(4)) decoder_1 (
    .out0(decoder_1_out0), .out1(decoder_1_out1), .out2(decoder_1_out2), .out3(decoder_1_out3),
    .out4(decoder_1_out4), .out5(decoder_1_out5), .out6(decoder_1_out6), .out7(MemWrt),
    .out8(decoder_1_out8), .out9(decoder_1_out9), .out10(decoder_1_out10), .out11(decoder_1_out11),
    .out12(decoder_1_out12), .out13(decoder_1_out13), .out14(decoder_1_out14), .out15(decoder_1_out15),
    .sel(counter_1_q));  // open: en
  or alu_imm (MUX1, decoder_1_out9, decoder_1_out11, decoder_1_out13, decoder_1_out15);
  or alu_normal (alu_normal_out, decoder_1_out8, decoder_1_out10, decoder_1_out12, decoder_1_out14);
  or alu (alu_out, MUX1, alu_normal_out);
  or ld_st (ld_st_out, MemRead, MemWrt);
  or Br (Br_out, decoder_1_out6, decoder_1_out4, decoder_1_out3, decoder_1_out2, bgt_2_out);
  or ld_st_alu (MUX5, alu_out, ld_st_out);
  not not_25 (MUX2[1], MUX5);
  or ld_st_jmp (MUX2[0], ld_st_out, decoder_1_out5);
  or or_4 (pcWrite, MUX5, decoder_1_out5, Br_out);
  or or_5 (WE, MemRead, alu_out);
  not not_26 (MUX3, MemRead);
  or or_6 (mux6, MUX5, decoder_1_out5);
  Multiplexer #(.width(3), .enable("false")) multiplexer_1 (
    .in0(3'b000), .in1(Instruction[16:14]), .out(BranchControlInput), .sel(Br_out));

  assign MUX4 = 1'b0;
  assign pcRead = 1'b1;
  assign wr = Instruction[13:10];

  // Notes on the sheet:
  //   sr2
  //   sr1
  //   dr
  //   Fetch1
  //   Fetch2
  //   beq
  //   bge
  //   blt
  //   jmp
  //   ble
  //   st
  //   add
  //   addi
  //   and
  //   andi
  //   or
  //   ori
  //   xor
  //   xori
  //   pc write dan 
  //   ld/st/alu/jump/branch
  //   ld/alu
  //   ld/st/alu/jmp
endmodule

module ZeroExtend4to5 (
  input  [3:0] in_1,
  output [4:0] out_2
);


  assign out_2 = {1'b1, in_1};
endmodule

module Comparator (
  input  B,
  input  A,
  input  A_B,
  input  A_B_2,
  input  A_B_3,
  output A_B_4,
  output A_B_5,
  output A_B_6
);

  wire and_1_out, and_2_out, and_3_out, and_5_out, and_6_out, and_7_out, not_1_out, not_2_out, not_3_out,
       not_4_out, or_1_out, or_3_out;

  not not_1 (not_1_out, B);
  not not_2 (not_2_out, A);
  and and_1 (and_1_out, not_1_out, A);
  and and_2 (and_2_out, B, not_2_out);
  or or_1 (or_1_out, and_1_out, and_2_out);
  not not_3 (not_3_out, or_1_out);
  and and_3 (and_3_out, A_B_2, and_1_out);
  and and_4 (A_B_5, not_3_out, A_B_2);
  or or_2 (A_B_4, A_B, and_3_out);
  and and_5 (and_5_out, and_2_out, A_B_2);
  and and_6 (and_6_out, not_3_out, A_B_3);
  and and_7 (and_7_out, A_B_3, and_1_out);
  or or_3 (or_3_out, and_5_out, and_2_out, and_6_out, and_7_out);
  not not_4 (not_4_out, A_B);
  and and_8 (A_B_6, or_3_out, not_4_out);
endmodule

module _18_Bit_Coparator (
  input  [17:0] Op1,
  input  [17:0] Op2,
  output A_B,
  output A_B_2,
  output A_B_3
);

  wire comparator_1_a_b_4, comparator_1_a_b_5, comparator_1_a_b_6, comparator_2_a_b_4, comparator_2_a_b_5,
       comparator_2_a_b_6, comparator_3_a_b_4, comparator_3_a_b_5, comparator_3_a_b_6, comparator_4_a_b_4,
       comparator_4_a_b_5, comparator_4_a_b_6, comparator_5_a_b_4, comparator_5_a_b_5, comparator_5_a_b_6,
       comparator_6_a_b_4, comparator_6_a_b_5, comparator_6_a_b_6, comparator_7_a_b_4, comparator_7_a_b_5,
       comparator_7_a_b_6, comparator_8_a_b_4, comparator_8_a_b_5, comparator_8_a_b_6, comparator_9_a_b_4,
       comparator_9_a_b_5, comparator_9_a_b_6, comparator_10_a_b_4, comparator_10_a_b_5, comparator_10_a_b_6,
       comparator_11_a_b_4, comparator_11_a_b_5, comparator_11_a_b_6, comparator_12_a_b_4,
       comparator_12_a_b_5, comparator_12_a_b_6, comparator_13_a_b_4, comparator_13_a_b_5,
       comparator_13_a_b_6, comparator_14_a_b_4, comparator_14_a_b_5, comparator_14_a_b_6,
       comparator_15_a_b_4, comparator_15_a_b_5, comparator_15_a_b_6, comparator_16_a_b_4,
       comparator_16_a_b_5, comparator_16_a_b_6, comparator_17_a_b_4, comparator_17_a_b_5,
       comparator_17_a_b_6;

  Comparator comparator_1 (
    .B(Op1[17]), .A(Op2[17]), .A_B(1'b0), .A_B_2(1'b1), .A_B_3(1'b0), .A_B_4(comparator_1_a_b_4),
    .A_B_5(comparator_1_a_b_5), .A_B_6(comparator_1_a_b_6));
  Comparator comparator_2 (
    .B(Op1[16]), .A(Op2[16]), .A_B(comparator_1_a_b_4), .A_B_2(comparator_1_a_b_5),
    .A_B_3(comparator_1_a_b_6), .A_B_4(comparator_2_a_b_4), .A_B_5(comparator_2_a_b_5),
    .A_B_6(comparator_2_a_b_6));
  Comparator comparator_3 (
    .B(Op1[15]), .A(Op2[15]), .A_B(comparator_2_a_b_4), .A_B_2(comparator_2_a_b_5),
    .A_B_3(comparator_2_a_b_6), .A_B_4(comparator_3_a_b_4), .A_B_5(comparator_3_a_b_5),
    .A_B_6(comparator_3_a_b_6));
  Comparator comparator_4 (
    .B(Op1[14]), .A(Op2[14]), .A_B(comparator_3_a_b_4), .A_B_2(comparator_3_a_b_5),
    .A_B_3(comparator_3_a_b_6), .A_B_4(comparator_4_a_b_4), .A_B_5(comparator_4_a_b_5),
    .A_B_6(comparator_4_a_b_6));
  Comparator comparator_5 (
    .B(Op1[13]), .A(Op2[13]), .A_B(comparator_4_a_b_4), .A_B_2(comparator_4_a_b_5),
    .A_B_3(comparator_4_a_b_6), .A_B_4(comparator_5_a_b_4), .A_B_5(comparator_5_a_b_5),
    .A_B_6(comparator_5_a_b_6));
  Comparator comparator_6 (
    .B(Op1[12]), .A(Op2[12]), .A_B(comparator_5_a_b_4), .A_B_2(comparator_5_a_b_5),
    .A_B_3(comparator_5_a_b_6), .A_B_4(comparator_6_a_b_4), .A_B_5(comparator_6_a_b_5),
    .A_B_6(comparator_6_a_b_6));
  Comparator comparator_7 (
    .B(Op1[11]), .A(Op2[11]), .A_B(comparator_6_a_b_4), .A_B_2(comparator_6_a_b_5),
    .A_B_3(comparator_6_a_b_6), .A_B_4(comparator_7_a_b_4), .A_B_5(comparator_7_a_b_5),
    .A_B_6(comparator_7_a_b_6));
  Comparator comparator_8 (
    .B(Op1[10]), .A(Op2[10]), .A_B(comparator_7_a_b_4), .A_B_2(comparator_7_a_b_5),
    .A_B_3(comparator_7_a_b_6), .A_B_4(comparator_8_a_b_4), .A_B_5(comparator_8_a_b_5),
    .A_B_6(comparator_8_a_b_6));
  Comparator comparator_9 (
    .B(Op1[9]), .A(Op2[9]), .A_B(comparator_8_a_b_4), .A_B_2(comparator_8_a_b_5), .A_B_3(comparator_8_a_b_6),
    .A_B_4(comparator_9_a_b_4), .A_B_5(comparator_9_a_b_5), .A_B_6(comparator_9_a_b_6));
  Comparator comparator_10 (
    .B(Op1[8]), .A(Op2[8]), .A_B(comparator_9_a_b_4), .A_B_2(comparator_9_a_b_5), .A_B_3(comparator_9_a_b_6),
    .A_B_4(comparator_10_a_b_4), .A_B_5(comparator_10_a_b_5), .A_B_6(comparator_10_a_b_6));
  Comparator comparator_11 (
    .B(Op1[7]), .A(Op2[7]), .A_B(comparator_10_a_b_4), .A_B_2(comparator_10_a_b_5),
    .A_B_3(comparator_10_a_b_6), .A_B_4(comparator_11_a_b_4), .A_B_5(comparator_11_a_b_5),
    .A_B_6(comparator_11_a_b_6));
  Comparator comparator_12 (
    .B(Op1[6]), .A(Op2[6]), .A_B(comparator_11_a_b_4), .A_B_2(comparator_11_a_b_5),
    .A_B_3(comparator_11_a_b_6), .A_B_4(comparator_12_a_b_4), .A_B_5(comparator_12_a_b_5),
    .A_B_6(comparator_12_a_b_6));
  Comparator comparator_13 (
    .B(Op1[5]), .A(Op2[5]), .A_B(comparator_12_a_b_4), .A_B_2(comparator_12_a_b_5),
    .A_B_3(comparator_12_a_b_6), .A_B_4(comparator_13_a_b_4), .A_B_5(comparator_13_a_b_5),
    .A_B_6(comparator_13_a_b_6));
  Comparator comparator_14 (
    .B(Op1[4]), .A(Op2[4]), .A_B(comparator_13_a_b_4), .A_B_2(comparator_13_a_b_5),
    .A_B_3(comparator_13_a_b_6), .A_B_4(comparator_14_a_b_4), .A_B_5(comparator_14_a_b_5),
    .A_B_6(comparator_14_a_b_6));
  Comparator comparator_15 (
    .B(Op1[3]), .A(Op2[3]), .A_B(comparator_14_a_b_4), .A_B_2(comparator_14_a_b_5),
    .A_B_3(comparator_14_a_b_6), .A_B_4(comparator_15_a_b_4), .A_B_5(comparator_15_a_b_5),
    .A_B_6(comparator_15_a_b_6));
  Comparator comparator_16 (
    .B(Op1[2]), .A(Op2[2]), .A_B(comparator_15_a_b_4), .A_B_2(comparator_15_a_b_5),
    .A_B_3(comparator_15_a_b_6), .A_B_4(comparator_16_a_b_4), .A_B_5(comparator_16_a_b_5),
    .A_B_6(comparator_16_a_b_6));
  Comparator comparator_17 (
    .B(Op1[1]), .A(Op2[1]), .A_B(comparator_16_a_b_4), .A_B_2(comparator_16_a_b_5),
    .A_B_3(comparator_16_a_b_6), .A_B_4(comparator_17_a_b_4), .A_B_5(comparator_17_a_b_5),
    .A_B_6(comparator_17_a_b_6));
  Comparator comparator_18 (
    .B(Op1[0]), .A(Op2[0]), .A_B(comparator_17_a_b_4), .A_B_2(comparator_17_a_b_5),
    .A_B_3(comparator_17_a_b_6), .A_B_4(A_B), .A_B_5(A_B_2), .A_B_6(A_B_3));
endmodule

module Branch_Control_Unit (
  input  [2:0] nzp,
  input  [17:0] op1,
  input  [17:0] op2,
  output MUX6
);

  wire n18_bit_coparator_1_a_b, n18_bit_coparator_1_a_b_2, n18_bit_coparator_1_a_b_3, or_1_out, or_2_out;

  _18_Bit_Coparator u_18_bit_coparator_1 (
    .Op1(op1), .Op2(op2), .A_B(n18_bit_coparator_1_a_b), .A_B_2(n18_bit_coparator_1_a_b_2),
    .A_B_3(n18_bit_coparator_1_a_b_3));
  or or_1 (or_1_out, n18_bit_coparator_1_a_b, n18_bit_coparator_1_a_b_2);
  or or_2 (or_2_out, n18_bit_coparator_1_a_b_2, n18_bit_coparator_1_a_b_3);
  Multiplexer #(.select(3)) multiplexer_1 (
    .in0(1'b0), .in1(n18_bit_coparator_1_a_b), .in2(n18_bit_coparator_1_a_b_2), .in3(or_1_out),
    .in4(n18_bit_coparator_1_a_b_3), .in5(1'b0), .in6(or_2_out), .in7(1'b0), .out(MUX6), .sel(nzp));  // open: en

  // Notes on the sheet:
  //   n,z,p input alacak, control unitten gelecek
  //   bgt
  //   beq
  //   bge
  //   blt
  //   ble
endmodule

module _18to10 (
  input  [17:0] in_1,
  output [9:0] out_2
);


  assign out_2 = in_1[9:0];
endmodule
